# Fritzing sketch PCB (saved by Fritzing 0.7.10b)
breadboards: 1

parts:
  IC1 = IC, DIP package, 40 pins [chip_label=IC spacing=600mil]
  J1 = female pin header, 8 pins [form="♀ (female)"]
  J2 = female pin header, 8 pins [form="♀ (female)"]
  J3 = female pin header, 8 pins [form="♀ (female)"]
  J4 = female pin header, 8 pins [form="♀ (female)"]
  J6 = female pin header, 8 pins [form="♀ (female)"]
  J5 = female pin header, 11 pins [form="♀ (female)"]
  XTAL1 = Crystal [frequency="16 Mhz" package=THT]
  C1 = Ceramic Capacitor [capacitance=100nF package="100 mil [THT, multilayer]"]
  C2 = Ceramic Capacitor [capacitance=100nF package="100 mil [THT, multilayer]"]
  J7 = female pin header, 4 pins [form="♀ (female)"]
  C3 = Ceramic Capacitor [capacitance=100nF package="100 mil [THT, multilayer]"]
  D1 = Rectifier Diode [part_number=1N4001 package="300 mil [THT]"]
  C4 = Ceramic Capacitor [capacitance=100nF package="100 mil [THT, multilayer]"]
  J10 = female pin header, 3 pins [form="♀ (female)"]
  J11 = female pin header, 3 pins [form="♀ (female)"]
  J12 = female pin header, 3 pins [form="♀ (female)"]
  J13 = female pin header, 3 pins [form="♀ (female)"]
  J14 = female pin header, 3 pins [form="♀ (female)"]
  J15 = female pin header, 3 pins [form="♀ (female)"]
  IC2 = IC, DIP package, 16 pins [chip_label=IC spacing=300mil]
  J16 = female pin header, 2 pins [form="♀ (female)"]
  J18 = female pin header, 2 pins [form="♀ (female)"]
  U1 = atmega168 [package="DIP28 [THT]"]
  J19 = female pin header, 2 pins [form="♀ (female)"]  # not connected
  C5 = Ceramic Capacitor [capacitance=100nF package="100 mil [THT, multilayer]"]
  D2 = Rectifier Diode [part_number=1N4001 package="300 mil [THT]"]
  C6 = Ceramic Capacitor [capacitance=100nF package="100 mil [THT, multilayer]"]
  J20 = female pin header, 6 pins [form="♀ (female)"]
  J21 = female pin header, 6 pins [form="♀ (female)"]
  J22 = female pin header, 6 pins [form="♀ (female)"]
  J23 = female pin header, 5 pins [form="♀ (female)"]
  J24 = female pin header, 5 pins [form="♀ (female)"]
  J25 = female pin header, 5 pins [form="♀ (female)"]
  J26 = female pin header, 6 pins [form="♀ (female)"]
  J27 = female pin header, 6 pins [form="♀ (female)"]
  J28 = female pin header, 6 pins [form="♀ (female)"]
  J29 = female pin header, 6 pins [form="♀ (female)"]
  J30 = female pin header, 6 pins [form="♀ (female)"]
  J31 = female pin header, 6 pins [form="♀ (female)"]
  R1 = Resistor [tolerance=±5% resistance=220 package=THT]
  R2 = Resistor [tolerance=±5% resistance=220 package=THT]
  J34 = female pin header, 4 pins [form="♀ (female)"]
  R3 = Resistor [tolerance=±5% resistance=220 package=THT]
  R4 = Resistor [tolerance=±5% resistance=220 package=THT]
  R5 = Resistor [tolerance=±5% resistance=220 package=THT]
  D3 = Rectifier Diode [part_number=1N4001 package="300 mil [THT]"]
  D4 = Rectifier Diode [part_number=1N4001 package="300 mil [THT]"]
  IC3 = IC, DIP package, 8 pins [chip_label=IC spacing=300mil]
  C7 = Ceramic Capacitor [capacitance=100nF package="100 mil [THT, multilayer]"]
  J35 = female pin header, 2 pins [form="♀ (female)"]
  C8 = Ceramic Capacitor [capacitance=100nF package="100 mil [THT, multilayer]"]
  U2 = Voltage Regulator - 5V [package="TO220 [THT]"]
  C9 = Ceramic Capacitor [capacitance=100nF package="100 mil [THT, multilayer]"]
  J36 = female pin header, 2 pins [form="♀ (female)"]
  LED1 = LED - 5mm [color="Red (633nm)" package="5 mm [THT]"]
  R6 = Resistor [tolerance=±5% resistance=220 package=THT]
  J37 = female pin header, 2 pins [form="♀ (female)"]
  J38 = female pin header, 4 pins [form="♀ (female)"]
  J33 = female pin header, 4 pins [form="♀ (female)"]
  J32 = female pin header, 4 pins [form="♀ (female)"]
  J8 = female pin header, 4 pins [form="♀ (female)"]
  J9 = female pin header, 4 pins [form="♀ (female)"]
  J39 = female pin header, 4 pins [form="♀ (female)"]
  J40 = female pin header, 2 pins [form="♀ (female)"]  # not connected
  S1 = Pushbutton [package="[THT]"]

nets (from the pcb view):
  N1: IC1.pin1, J5.pin1
  N2: IC1.pin2, J5.pin2
  N3: IC1.pin3, J5.pin3
  N4: IC1.pin4, J5.pin4
  N5: IC1.pin5, J5.pin5
  N6: IC1.pin6, J5.pin6, IC3.pin5
  N7: IC1.pin7, J5.pin7, IC3.pin6
  N8: IC1.pin8, J5.pin8, IC3.pin7
  N9: IC1.pin9, J5.pin9, S1.Pin_3, S1.Pin_4
  N10: IC1.pin10, J4.pin1, J4.pin8, J5.pin10
  N11: IC1.pin11, IC1.pin31, J2.pin1, J2.pin8, J6.pin1, J6.pin8, J5.pin11, C1.1, C2.0, C3.1, C4.0, J11.pin1, J11.pin3, J14.pin1, J14.pin3, U1.Pin_8, U1.Pin_22, C5.0, C6.0, J28.pin1, J28.pin6, J31.pin1, J31.pin6, J34.pin1, D3.anode, D4.anode, IC3.pin4, J35.pin2, C8.1, U2.GND, C9.1, J36.pin2, LED1.cathode, J8.pin1, J8.pin4
  N12: IC1.pin12, XTAL1.pin_0, C1.0
  N13: IC1.pin13, XTAL1.pin_1, C2.1
  N14: IC1.pin14, J7.pin1
  N15: IC1.pin15, J7.pin2
  N16: IC1.pin16, J7.pin3
  N17: IC1.pin17, J7.pin4
  N18: IC1.pin18, IC2.pin1
  N19: IC1.pin19, IC2.pin9
  N20: IC1.pin20, IC2.pin15
  N21: IC1.pin21, J13.pin3
  N22: IC1.pin22, J13.pin2
  N23: IC1.pin23, J13.pin1
  N24: IC1.pin24, IC2.pin2
  N25: IC1.pin25, IC2.pin7
  N26: IC1.pin26, IC2.pin10
  N27: IC1.pin27, J10.pin3
  N28: IC1.pin28, J10.pin2
  N29: IC1.pin29, J10.pin1
  N30: IC1.pin30, D1.cathode
  N31: IC1.pin32, C3.0
  N32: IC1.pin33, J1.pin8
  N33: IC1.pin34, J1.pin7
  N34: IC1.pin35, J1.pin6
  N35: IC1.pin36, J1.pin5
  N36: IC1.pin37, J1.pin4
  N37: IC1.pin38, J1.pin3
  N38: IC1.pin39, J1.pin2
  N39: IC1.pin40, J1.pin1
  N40: J3.pin1, J3.pin8, J4.pin3, D1.anode, C4.1, J12.pin1, J12.pin3, J15.pin1, J15.pin3, U1.Pin_7, J22.pin5, J24.pin1, J24.pin5, J27.pin1, J27.pin6, J30.pin1, J30.pin6, J34.pin4, R5.Pin_1, IC3.pin8, C7.1, J9.pin1, J9.pin4
  N41: J4.pin7, U2.output_voltage, C9.0, J36.pin1, R6.Pin_0
  N42: IC2.pin3, J18.pin2
  N43: IC2.pin4, IC2.pin5, IC2.pin12, IC2.pin13, J37.pin1
  N44: IC2.pin6, J18.pin1
  N45: IC2.pin8, J37.pin2
  N46: IC2.pin11, J16.pin2
  N47: IC2.pin14, J16.pin1
  N48: IC2.pin16, D2.anode, C6.1
  N49: U1.Pin_1, J26.pin1, J39.pin4
  N50: U1.Pin_2, J26.pin2
  N51: U1.Pin_3, J26.pin3
  N52: U1.Pin_4, J26.pin4
  N53: U1.Pin_5, J26.pin5
  N54: U1.Pin_6, J26.pin6
  N55: U1.Pin_9, J29.pin1
  N56: U1.Pin_10, J29.pin2
  N57: U1.Pin_11, J29.pin3
  N58: U1.Pin_12, J29.pin4
  N59: U1.Pin_13, J29.pin5
  N60: U1.Pin_14, J29.pin6
  N61: U1.Pin_15, J23.pin5
  N62: U1.Pin_16, J23.pin4
  N63: U1.Pin_17, J23.pin3, J39.pin1
  N64: U1.Pin_18, J23.pin2, J39.pin2
  N65: U1.Pin_19, J23.pin1, J39.pin3
  N66: U1.Pin_20, D2.cathode
  N67: U1.Pin_21, C5.1
  N68: U1.Pin_23, J20.pin6
  N69: U1.Pin_24, J20.pin5
  N70: U1.Pin_25, J20.pin4
  N71: U1.Pin_26, J20.pin3
  N72: U1.Pin_27, J20.pin2, R1.Pin_0, J32.pin1, J32.pin3
  N73: U1.Pin_28, J20.pin1, R2.Pin_0, J33.pin1, J33.pin3
  N74: J21.pin1, J21.pin6, J25.pin1, J25.pin5
  N75: J22.pin1, J22.pin6, R1.Pin_1, R2.Pin_1
  N76: J34.pin2, R3.Pin_0, D4.cathode
  N77: J34.pin3, R4.Pin_0, D3.cathode
  N78: R3.Pin_1, IC3.pin2
  N79: R4.Pin_1, IC3.pin3
  N80: IC3.pin1, J38.pin1, S1.Pin_2
  N81: J35.pin1, C8.0, U2.input_voltage
  N82: LED1.anode, R6.Pin_1
