# Fritzing sketch tact (saved by Fritzing 0.6.4b)
breadboards: 1

parts:
  VCC1 = Battery
  R1 = Resistor [tolerance=±5% resistance=220 package=THT]
  J1 = female pin header, 1 pin [form="♀ (female)"]
  J2 = female pin header, 1 pin [form="♀ (female)"]
  R2 = Resistor [tolerance=±5% resistance=220 package=THT]

nets:
  N1: VCC1.+, R1.Pin_1, R2.Pin_1
  N2: R1.Pin_0, J1.pin1
  N3: J2.pin1, R2.Pin_0
